# Fritzing sketch WiringMain (saved by Fritzing 0.9.2b)

parts:
  Part1 = Arduino Uno (Rev3)
  LCD1 = LCD screen
  IR1 = TSOP312.., 314.. [package=THT]
  Power_plug1 = Power plug
  U1 = SWITCH-SPST-2 [package=switch-spst-vertical]
  LED2 = LED - 5mm [color="Blue (505nm)" package="5 mm [THT]"]
  R6 = Resistor [tolerance=±5% resistance=1k package=THT]  # not connected
  R7 = Rotary Potentiometer (Small) [maximum_resistance=100kΩ package=THT]

nets:
  N1: Part1.A5/SCL, IR1.GND
  N2: Part1.D2, LCD1.RS
  N3: Part1.D3_PWM, LCD1.E
  N4: Part1.D4, LCD1.DB4
  N5: Part1.D5_PWM, LCD1.DB5
  N6: Part1.D6_PWM, LCD1.DB6
  N7: Part1.D7, LCD1.DB7
  N8: Part1.5V, IR1.Data
  N9: Part1.GND, IR1.Vs, LED2.cathode
  N10: Part1.VIN, U1.P
  N11: LCD1.V0, R7.wiper
  N12: Power_plug1.VCC, U1.O

notes:
  To String LED Cathodes
  (See LED Wiring)
  E - Yellow
  B - Green
  G - Blue
  D - White
  A - Red
  E - Black
  E A D G B E
  To Fret 220 Ohm Anode Resistors
  (See LED Wiring)
  Yellow Fret 1
  Green Fret 2
  Blue Fret 3
  White Fret 4
  Grey Fret 5
  AX-1838HS
  1 - Output
  2 - Gnd
  3 - +5
  9V In
  10k Ohm Potentiometer
  LED Is Built Into The Switch.
  1K OhmResistor.
  From pwr jack, (black) Gnd wires goes to Arduino Gnd, and to switch LED
  From switch, Gnd wire goes to LCD and to IR sensor.
  Gnd, +5
